# Fritzing sketch Chinstick Circuit Diagram (saved by Fritzing 0.7.7b)
breadboards: 1

parts:
  Arduino1 = Arduino
  L_Right = Pushbutton [package=THT]
  L_Down = Pushbutton [package=THT]
  L_Left = Pushbutton [package=THT]
  L_Up = Pushbutton [package=THT]
  R_Left = Pushbutton [package=THT]
  R_Right = Pushbutton [package=THT]
  R_Down = Pushbutton [package=THT]
  R_Up = Pushbutton [package=THT]
  LED1 = LED - 5mm [color="Red (633nm)" package="5 mm [THT]"]
  LED2 = LED - 5mm [color="Red (633nm)" package="5 mm [THT]"]
  LED3 = LED - 5mm [color="Red (633nm)" package="5 mm [THT]"]
  LED4 = LED - 5mm [color="Red (633nm)" package="5 mm [THT]"]
  R1 = Resistor [tolerance=±5% resistance=220 package=THT]
  R2 = Resistor [tolerance=±5% resistance=220 package=THT]
  R3 = Resistor [tolerance=±5% resistance=220 package=THT]
  R4 = Resistor [tolerance=±5% resistance=220 package=THT]

nets:
  N1: Arduino1.D13, R4.Pin_0
  N2: Arduino1.D12, R3.Pin_0
  N3: Arduino1.D11, R2.Pin_0
  N4: Arduino1.D10, R1.Pin_0
  N5: Arduino1.D9, L_Right.leg1
  N6: Arduino1.D8, L_Up.leg1
  N7: Arduino1.D7, L_Left.leg1
  N8: Arduino1.D6, L_Down.leg1
  N9: Arduino1.D4, R_Down.leg1
  N10: Arduino1.D3, R_Up.leg1
  N11: Arduino1.D2, R_Left.leg1
  GND: L_Right.leg0, R_Right.leg0, LED1.cathode, LED2.cathode, LED3.cathode, LED4.cathode
  N12: LED1.anode, R1.Pin_1
